# Fritzing sketch NodeMCU-Robot (saved by Fritzing 0.9.3b)
breadboards: 1

parts:
  U1 = NodeMCU V1.0  # not connected
  Part1 = HTU21D Breakout
  U2 = SWITCH-SPST-2 [package=switch-spst-vertical]
  R1 = Photocell (LDR) [package=THT]
  part = Resistor [tolerance=±5% resistance=10k package="1206 [SMD]"]
  J5 = male pin header, 11 pins [form="♂ (male)"]  # not connected
  J6 = male pin header, 11 pins [form="♂ (male)"]
  J7 = male pin header, 11 pins [form="♂ (male)"]
  J8 = male pin header, 11 pins [form="♂ (male)"]
  J9 = male pin header, 3 pins [form="♂ (male)"]
  J10 = male pin header, 3 pins [form="♂ (male)"]
  J11 = male pin header, 3 pins [form="♂ (male)"]  # not connected
  M1 = DC Motor  # not connected
  M2 = DC Motor  # not connected
  VCC1 = 4 x AAA Battery Mount

nets:
  N1: Part1.SCL, J8.pin5
  N2: Part1.SDA, J8.pin6
  N3: Part1.GND, part.Pin_0, J6.pin11
  N4: Part1.3.3V, R1.pin_1, J7.pin11
  N5: U2.O, VCC1.+
  N6: R1.pin_0, part.Pin_1, J10.pin3
  N7: J9.pin1, J9.pin2

notes:
  8  7  6  5  4  3  2  1  0
  GND
  VIN
  VM
  B+
  B-
  A+
  A-
  A0

custom parts:
  NodeMCU V1.0: ESP8266 based NodeMCU V1.0
  HTU21D Breakout: This is a breadboard friendly breakout board for the Measurement Specialties high-precision, low-power digital humidity sensor.
